# Fritzing sketch beehive monitor feather (saved by Fritzing 0.9.3b)
breadboards: 2

parts:
  Onderdeel2 = Adafruit Feather M0 WINC1500 [part_number="Adafruit #3010"]
  R1 = Resistor [tolerance=±5% resistance=220 package="2010 [SMD]"]
  R2 = Resistor [tolerance=±5% resistance=220 package="2010 [SMD]"]
  J1 = female pin header, 2 pins [form="♀ (female)"]
  R3 = Resistor [tolerance=±5% resistance=220 package="2010 [SMD]"]
  R4 = Resistor [tolerance=±5% resistance=220 package="2010 [SMD]"]
  R5 = Resistor [tolerance=±5% resistance=220 package="2010 [SMD]"]
  Onderdeel3 = HX711 Weighing Sensor Module
  Onderdeel4 = HX711 Weighing Sensor Module

nets:
  N1: Onderdeel2.A4, R5.Pin_0
  N2: Onderdeel2.A3, R4.Pin_0
  N3: Onderdeel2.A2, R3.Pin_0
  N4: Onderdeel2.A0, J1.pin1
  N5: Onderdeel2.+3V3, R1.Pin_1, R2.Pin_1, J1.pin2, R3.Pin_1, R4.Pin_1, R5.Pin_1
  N6: Onderdeel2.D12, Onderdeel3.DO/RX
  N7: Onderdeel2.D11, Onderdeel3.CK/TX
  N8: Onderdeel2.D6, Onderdeel4.CK/TX
  N9: Onderdeel2.SCL, R2.Pin_0
  N10: Onderdeel2.SDA, R1.Pin_0

custom parts:
  Adafruit Feather M0 WINC1500: This is the Adafruit Feather M0 WiFi w/ATWINC1500 - our take on an 'all-in-one' Arduino-compatible + high speed, reliable WiFi with built in USB and battery charging. Its an Adafruit Feather M0 with a WiFi module, ready to rock! Connect your Feather to the Internet with this fine new FCC-certified WiFi module from Atmel. This 802.11bgn-capable WiFi module is the best new thing for networking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
