# Fritzing sketch beehive monitor3 (saved by Fritzing 0.9.3b)
circuit board: 6.60401cm x 6.61812cm
circuit board: 10cm x 6cm
breadboards: 2

parts:
  S1 = Toggle Switch [package=THT]
  Onderdeel2 = Arduino MKR1000
  R1 = Resistor [tolerance=±5% resistance=4.7k package=THT]
  R2 = Resistor [tolerance=±5% resistance=4.7k package=THT]
  J3 = male pin header, 5 pins [form="♂ (male)"]
  J7 = male pin header, 3 pins [form="♂ (male)"]
  J6 = male pin header, 3 pins [form="♂ (male)"]
  J5 = male pin header, 3 pins [form="♂ (male)"]
  J4 = male pin header, 4 pins [form="♂ (male)"]
  J2 = male pin header, 4 pins [form="♂ (male)"]
  R3 = Resistor [tolerance=±5% resistance=220 package=THT]
  R4 = Resistor [tolerance=±5% resistance=220 package=THT]
  Onderdeel3 = Barometric Pressure Sensor - BMP085 Breakout

nets:
  N1: S1.COM, Onderdeel2.GND, J3.pin2, R4.Pin_0
  N2: S1.L2, Onderdeel2.D7
  N3: Onderdeel2.D2_PWM, R2.Pin_0, J4.pin3
  N4: Onderdeel2.D3_PWM, R1.Pin_1, J7.pin1, J6.pin1, J5.pin1
  N5: Onderdeel2.D4_PWM, J2.pin3
  N6: Onderdeel2.D5_PWM, J2.pin4
  N7: Onderdeel2.D8_MOSI, J3.pin5
  N8: Onderdeel2.D9_SCK, J3.pin4
  N9: Onderdeel2.D10_MISO, J3.pin3
  N10: Onderdeel2.A0/DAC0, Onderdeel3.EOC
  N11: Onderdeel2.A2, Onderdeel3.VCC
  N12: Onderdeel2.A4/SDA, R3.Pin_0, R4.Pin_1
  N13: Onderdeel2.VIN, J3.pin1
  N14: R1.Pin_0, R2.Pin_1, J7.pin3, J6.pin3, J5.pin3, J4.pin4, J2.pin1
  N15: J7.pin2, J6.pin2, J5.pin2, J4.pin1, J2.pin2

notes:
  DS2
  Scale
  DHT22

custom parts:
  Arduino MKR1000: MKR1000 is a powerful board that combines the functionality of the Zero and the Wi-Fi Shield. It is the ideal solution for makers wanting to design IoT projects with minimal previous experience in networking
